# Fritzing sketch Ball1 (saved by Fritzing 0.9.3b)
breadboards: 1

parts:
  Componente1 = Arduino Mega 2560 (Rev3)
  R1 = Resistor [tolerance=±5% resistance=220 package=THT]  # not connected
  R2 = Resistor [tolerance=±5% resistance=220 package=THT]  # not connected
  R3 = Resistor [tolerance=±5% resistance=220 package=THT]  # not connected
  R4 = Resistor [tolerance=±5% resistance=220 package=THT]  # not connected
  R5 = Resistor [tolerance=±5% resistance=220 package=THT]  # not connected
  R6 = Resistor [tolerance=±5% resistance=220 package=THT]  # not connected
  R7 = Resistor [tolerance=±5% resistance=220 package=THT]  # not connected
  R8 = Resistor [tolerance=±5% resistance=220 package=THT]  # not connected
  R9 = Resistor [tolerance=±5% resistance=220 package=THT]  # not connected
  R10 = Resistor [tolerance=±5% resistance=220 package=THT]  # not connected
  R11 = Resistor [tolerance=±5% resistance=220 package=THT]  # not connected
  R12 = Resistor [tolerance=±5% resistance=220 package=THT]  # not connected
  R13 = Resistor [tolerance=±5% resistance=220 package=THT]
  R14 = Resistor [tolerance=±5% resistance=220 package=THT]
  R15 = Resistor [tolerance=±5% resistance=220 package=THT]
  S1 = Pushbutton [package="[THT]"]
  R16 = Trimmer Potentiometer [maximum_resistance=100kΩ package=THT]  # not connected
  J1 = Basic Servo
  RGB_LED_(common_anode) = RGB LED (com. anode, rbg) [package="5 mm [THT]"]

nets:
  GND: Componente1.GND, J1.gnd
  N1: Componente1.D8_PWM, J1.pulse
  5V: Componente1.5V, J1.vcc, RGB_LED_(common_anode).common_anode
  N2: Componente1.D30, R13.Pin_0
  N3: Componente1.D31, R14.Pin_0
  N4: Componente1.D32, R15.Pin_0
  N5: R13.Pin_1, RGB_LED_(common_anode).blue_cathode
  N6: R14.Pin_1, RGB_LED_(common_anode).green_cathode
  N7: R15.Pin_1, RGB_LED_(common_anode).red_cathode
  N8: S1.Pin_1, S1.Pin_2
  N9: S1.Pin_3, S1.Pin_4

notes:
  RGB LED BALL 1
