# Fritzing sketch PotenandButton (saved by Fritzing 0.9.3b)
breadboards: 1

parts:
  Componente1 = Arduino Mega 2560 (Rev3)
  R1 = Resistor [tolerance=±5% resistance=220 package=THT]  # not connected
  R2 = Resistor [tolerance=±5% resistance=220 package=THT]  # not connected
  R3 = Resistor [tolerance=±5% resistance=220 package=THT]  # not connected
  R4 = Resistor [tolerance=±5% resistance=220 package=THT]  # not connected
  R5 = Resistor [tolerance=±5% resistance=220 package=THT]  # not connected
  R6 = Resistor [tolerance=±5% resistance=220 package=THT]  # not connected
  R7 = Resistor [tolerance=±5% resistance=220 package=THT]  # not connected
  R8 = Resistor [tolerance=±5% resistance=220 package=THT]  # not connected
  R9 = Resistor [tolerance=±5% resistance=220 package=THT]  # not connected
  R10 = Resistor [tolerance=±5% resistance=220 package=THT]  # not connected
  R11 = Resistor [tolerance=±5% resistance=220 package=THT]  # not connected
  R12 = Resistor [tolerance=±5% resistance=220 package=THT]  # not connected
  R13 = Resistor [tolerance=±5% resistance=220 package=THT]  # not connected
  R14 = Resistor [tolerance=±5% resistance=220 package=THT]  # not connected
  R15 = Resistor [tolerance=±5% resistance=220 package=THT]  # not connected
  S1 = Pushbutton [package="[THT]"]
  R16 = Trimmer Potentiometer [maximum_resistance=100kΩ package=THT]
  R17 = Resistor [tolerance=±5% resistance=10k package=THT]

nets:
  N1: Componente1.A0, R16.wiper
  N2: Componente1.GND, S1.Pin_1, S1.Pin_2, R16.leg1
  N3: Componente1.5V, R16.leg2, R17.Pin_0
  N4: Componente1.D7_PWM, S1.Pin_3, S1.Pin_4, R17.Pin_1

notes:
  POTENTIOMETER AND BUTTON
